// Logisim project Project1.circ as structural Verilog: 2 circuits, main circuit 1BitAdder
module _1BitAdder (
  input  X,
  input  Y,
  input  Cin,
  output Sum,
  output Cout
);

  wire and_1_out, and_2_out, and_3_out, and_4_out, and_5_out, and_6_out, and_7_out, not_1_out, not_2_out,
       not_3_out, not_4_out, not_5_out, not_6_out;

  not not_1 (not_1_out, X);
  not not_2 (not_2_out, Y);
  not not_3 (not_3_out, X);
  not not_4 (not_4_out, Cin);
  not not_5 (not_5_out, Y);
  not not_6 (not_6_out, Cin);
  and and_1 (and_1_out, X, Y);
  and and_2 (and_2_out, Y, Cin);
  and and_3 (and_3_out, X, Cin);
  and and_4 (and_4_out, not_1_out, not_2_out, Cin);
  and and_5 (and_5_out, not_3_out, Y, not_4_out);
  and and_6 (and_6_out, X, Y, Cin);
  and and_7 (and_7_out, X, not_5_out, not_6_out);
  or or_1 (Cout, and_1_out, and_2_out, and_3_out);
  or or_2 (Sum, and_4_out, and_5_out, and_6_out, and_7_out);
endmodule

module _3BitAdder (
  input  X2,
  input  X1,
  input  X0,
  input  Y2,
  input  Y1,
  input  Y0,
  input  Cin,
  output Cout,
  output S2,
  output S1,
  output S0
);

  wire n1bitadder_2_cout, n1bitadder_3_cout;

  _1BitAdder u_1bitadder_1 (.X(X2), .Y(Y2), .Cin(n1bitadder_2_cout), .Sum(S2), .Cout(Cout));
  _1BitAdder u_1bitadder_2 (.X(X1), .Y(Y1), .Cin(n1bitadder_3_cout), .Sum(S1), .Cout(n1bitadder_2_cout));
  _1BitAdder u_1bitadder_3 (.X(X0), .Y(Y0), .Cin(Cin), .Sum(S0), .Cout(n1bitadder_3_cout));
endmodule
