// Logisim project Project 2.circ as structural Verilog: 3 circuits, main circuit main
module main (
);

  wire button_1_out;
  wire [3:0] decoder_1_abcd, decoder_1_efg, mod10_count_1_out_2;

  Button button_1 (.out(button_1_out));
  Mod10_Count mod10_count_1 (.Clk(button_1_out), .out_2(mod10_count_1_out_2));
  Decoder decoder_1 (.X3(mod10_count_1_out_2), .ABCD(decoder_1_abcd), .EFG(decoder_1_efg));
  _7_Segment_Display u_7_segment_display_1 (
    .g(decoder_1_efg[2]), .f(decoder_1_efg[1]), .a(decoder_1_abcd[0]), .b(decoder_1_abcd[1]),
    .e(decoder_1_efg[0]), .d(decoder_1_abcd[3]), .c(decoder_1_abcd[2]), .dp(decoder_1_efg[3]));
endmodule

module Decoder (
  input  [3:0] X3,
  output [3:0] ABCD,
  output [3:0] EFG
);

  wire and_1_out, and_2_out, and_3_out, and_4_out, and_5_out, and_6_out, and_7_out, and_8_out, and_9_out,
       and_10_out, and_11_out, and_12_out, and_13_out, and_14_out, and_15_out, and_16_out, and_17_out,
       and_18_out, and_19_out, and_20_out, and_21_out, and_22_out, and_23_out, and_24_out, and_25_out,
       and_26_out, and_27_out, not_1_out, not_2_out, not_3_out, not_4_out, not_5_out, not_6_out, not_7_out,
       not_8_out, not_9_out, not_10_out, not_11_out, not_12_out, not_13_out, not_14_out, not_15_out,
       not_16_out, not_17_out, not_18_out, not_19_out, not_20_out, not_21_out, not_22_out, not_23_out,
       not_24_out, not_25_out, not_26_out, not_27_out, not_28_out, not_29_out, not_30_out, not_31_out,
       not_32_out, not_33_out, not_34_out;

  and and_1 (and_1_out, X3[2], X3[0]);
  not not_1 (not_1_out, X3[2]);
  and and_2 (and_2_out, not_1_out, not_2_out);
  not not_2 (not_2_out, X3[0]);
  not not_3 (not_3_out, X3[3]);
  and and_3 (and_3_out, not_3_out, X3[1], X3[0]);
  not not_4 (not_4_out, X3[2]);
  not not_5 (not_5_out, X3[1]);
  and and_4 (and_4_out, X3[3], not_5_out, X3[0]);
  not not_6 (not_6_out, X3[3]);
  and and_5 (and_5_out, not_6_out, not_7_out, not_8_out);
  not not_7 (not_7_out, X3[1]);
  not not_8 (not_8_out, X3[0]);
  not not_9 (not_9_out, X3[3]);
  and and_6 (and_6_out, not_9_out, X3[2]);
  and and_7 (and_7_out, X3[3], not_10_out);
  not not_10 (not_10_out, X3[2]);
  not not_11 (not_11_out, X3[1]);
  and and_8 (and_8_out, not_11_out, X3[0]);
  not not_12 (not_12_out, X3[3]);
  and and_9 (and_9_out, not_12_out, not_13_out);
  not not_13 (not_13_out, X3[1]);
  not not_14 (not_14_out, X3[3]);
  and and_10 (and_10_out, not_14_out, X3[0]);
  not not_15 (not_15_out, X3[1]);
  and and_11 (and_11_out, X3[3], not_15_out, not_16_out);
  not not_16 (not_16_out, X3[0]);
  and and_12 (and_12_out, X3[2], not_17_out, X3[0]);
  not not_17 (not_17_out, X3[1]);
  not not_18 (not_18_out, X3[2]);
  and and_13 (and_13_out, not_18_out, X3[1], X3[0]);
  not not_19 (not_19_out, X3[3]);
  not not_20 (not_20_out, X3[2]);
  and and_14 (and_14_out, not_19_out, not_20_out, not_21_out);
  not not_21 (not_21_out, X3[0]);
  and and_15 (and_15_out, X3[2], X3[1], not_22_out);
  not not_22 (not_22_out, X3[0]);
  and and_16 (and_16_out, X3[1], not_23_out);
  not not_23 (not_23_out, X3[0]);
  and and_17 (and_17_out, X3[3], X3[2]);
  not not_24 (not_24_out, X3[2]);
  and and_18 (and_18_out, not_24_out, not_25_out);
  not not_25 (not_25_out, X3[0]);
  and and_19 (and_19_out, X3[3], X3[1]);
  and and_20 (and_20_out, X3[2], not_26_out);
  not not_26 (not_26_out, X3[1]);
  not not_27 (not_27_out, X3[1]);
  and and_21 (and_21_out, not_27_out, not_28_out);
  not not_28 (not_28_out, X3[0]);
  and and_22 (and_22_out, X3[2], not_29_out);
  not not_29 (not_29_out, X3[0]);
  and and_23 (and_23_out, X3[3], not_30_out);
  not not_30 (not_30_out, X3[2]);
  and and_24 (and_24_out, X3[1], not_31_out);
  not not_31 (not_31_out, X3[0]);
  and and_25 (and_25_out, X3[3], X3[1]);
  not not_32 (not_32_out, X3[2]);
  and and_26 (and_26_out, not_32_out, X3[1]);
  not not_33 (not_33_out, X3[3]);
  and and_27 (and_27_out, not_33_out, X3[2], not_34_out);
  not not_34 (not_34_out, X3[1]);
  or or_1 (ABCD[0], X3[3], X3[1], and_1_out, and_2_out);
  or or_2 (ABCD[1], and_3_out, not_4_out, and_4_out, and_5_out);
  or or_3 (ABCD[2], and_6_out, and_7_out, and_8_out, and_9_out, and_10_out);
  or or_4 (ABCD[3], and_11_out, and_12_out, and_13_out, and_14_out, and_15_out);
  or or_5 (EFG[0], and_16_out, and_17_out, and_18_out, and_19_out);
  or or_6 (EFG[1], X3[3], and_20_out, and_21_out, and_22_out);
  or or_7 (EFG[2], and_23_out, and_24_out, and_25_out, and_26_out, and_27_out);
endmodule

module Mod10_Count (
  input  Clk,
  output [3:0] out_2
);

  wire and_1_out, j_k_ff_1_q, j_k_ff_2_q, j_k_ff_3_q, j_k_ff_4_q;

  J_K_Flip_Flop j_k_ff_1 (.J(Clk), .clk(Clk), .K(Clk), .Q(j_k_ff_1_q), .preset(and_1_out));  // open: Qn, en, reset
  J_K_Flip_Flop j_k_ff_2 (
    .J(Clk), .clk(j_k_ff_1_q), .K(Clk), .Q(j_k_ff_2_q), .preset(and_1_out));  // open: Qn, en, reset
  J_K_Flip_Flop j_k_ff_3 (
    .J(Clk), .clk(j_k_ff_2_q), .K(Clk), .Q(j_k_ff_3_q), .preset(and_1_out));  // open: Qn, en, reset
  J_K_Flip_Flop j_k_ff_4 (
    .J(Clk), .clk(j_k_ff_3_q), .K(Clk), .Q(j_k_ff_4_q), .preset(and_1_out));  // open: Qn, en, reset
  not not_1 (out_2[0], j_k_ff_1_q);
  not not_2 (out_2[1], j_k_ff_2_q);
  not not_3 (out_2[2], j_k_ff_3_q);
  not not_4 (out_2[3], j_k_ff_4_q);
  and and_1 (and_1_out, out_2[1], out_2[3]);
endmodule
